# Fritzing sketch CustomBadge_LabsCon_V2 (saved by Fritzing 0.9.10b)
circuit board: 8.8cm x 7cm

parts:
  Feather_M0_Exp = Adafruit Feather M0 Express [part_number="Adafruit #3403"]
  MX1 = Cherry MX Keyswitch Simple
  MX2 = Cherry MX Keyswitch Simple
  1_54_ST7789 = Adafruit 1.54inch 240x240 IPS TFT [part_number="Adafruit #3787"]

nets:
  GND: Feather_M0_Exp.GND, MX1.pin_1, MX2.pin_1, 1_54_ST7789.GND
  N1: Feather_M0_Exp.MISO, 1_54_ST7789.MISO
  N2: Feather_M0_Exp.MOSI, 1_54_ST7789.MOSI
  N3: Feather_M0_Exp.SCK, 1_54_ST7789.SCK
  N4: Feather_M0_Exp.A4, 1_54_ST7789.TFTCS
  +3V3: Feather_M0_Exp.+3V3, 1_54_ST7789.VIN
  N5: Feather_M0_Exp.D12, 1_54_ST7789.CARDCS
  N6: Feather_M0_Exp.D11, 1_54_ST7789.TFTDC
  N7: Feather_M0_Exp.D10, 1_54_ST7789.TFTRST
  N8: Feather_M0_Exp.D6, MX1.pin_2
  N9: Feather_M0_Exp.D5, MX2.pin_2

notes:
  Labs Con 2022 - BLove

custom parts:
  Adafruit Feather M0 Express: We love all our Feathers equally, but this Feather is very special. It's our first Feather that is specifically designed for use with CircuitPython! CircuitPython is our beginner-oriented flavor of MicroPython - and as the name hints at, its a small but full-featured version of the popular Python programming language specifically for use with circuitry and electronics. That doesn't mean you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
  Cherry MX Keyswitch Simple: Cherry MX Keyswitch button for keyboards
  Adafruit 1.54inch 240x240 IPS TFT: We've been looking for a display like this for a long time - it's only 1.5" diagonal but has a high density 220 ppi, 240x240 pixel display with full-angle viewing. It looks a lot like our 1.44" 128x128 display, but has 4x as many pixels and looks great at any angle. We've seen displays of this caliber used in smartwatches and small electronic devices but they've always been MIPI interface.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
